# Fritzing sketch arduino_esp2866_adapter (saved by Fritzing 0.9.2b)
circuit board: 5.3cm x 1.8cm
breadboards: 1

parts:
  D2 = Rectifier Diode [part_number=1N4001 package="300 mil [THT]"]
  R1 = Resistor [tolerance=±5% resistance=100k package=THT]
  3_3V = male pin header, 3 pins [form="♂ (male)"]
  J2 = female pin header, 2 pins [form="♀ (female)"]
  D3 = Rectifier Diode [part_number=1N4001 package="300 mil [THT]"]
  U2 = ESP8266 WiFi Module [part_number=ESP8266]
  J3 = female pin header, 2 pins [form="♀ (female)"]
  J1 = female pin header, 4 pins [form="♀ (female)"]
  Pad1 = Pad [width=1 height=1 connect=center]
  CD4048B2 = CD4048B [part_number=CD4050 package="DIP (Dual Inline) [THT]"]

nets:
  N1: D2.cathode, 3_3V.pin1, D3.anode
  N2: D2.anode, J2.pin2, J3.pin2
  N3: R1.Pin_0, 3_3V.pin3, D3.cathode
  GND: R1.Pin_1, J2.pin1, U2.GND, J3.pin1, CD4048B2.VSS
  N4: 3_3V.pin2, U2.VCC, U2.GPIO_0, U2.GPIO_2, Pad1.pad, CD4048B2.J
  N5: U2.RXD, CD4048B2.E
  N6: U2.RST, CD4048B2.G
  N7: U2.CH_PD, CD4048B2.Kd
  N8: U2.TXD, J1.pin4
  N9: J1.pin1, CD4048B2.H
  N10: J1.pin2, CD4048B2.F
  N11: J1.pin3, CD4048B2.Kb

notes:
  Alex Porto

custom parts:
  ESP8266 WiFi Module: Generic WiFi Module based on the ESP8266 with onboard PCB antenna and UART communications
